# Fritzing sketch ESP_client (saved by Fritzing 0.9.6b)
circuit board: 6.74599cm x 4.7627cm

parts:
  ITG/MPU6065 = InvenSense MPU6050
  Node_MCU_1_(ESP-12E_Module) = Gizwits WiFi Witty ESP-12F

nets:
  VCC: ITG/MPU6065.VCC, Node_MCU_1_(ESP-12E_Module).VCC
  GND: ITG/MPU6065.GND, Node_MCU_1_(ESP-12E_Module).GND
  N1: ITG/MPU6065.SCL, Node_MCU_1_(ESP-12E_Module).GPIO5
  N2: ITG/MPU6065.SDA, Node_MCU_1_(ESP-12E_Module).GPIO4
